// Logisim project HalfAdder.circ as structural Verilog: 2 circuits, main circuit main
module main (
  input  in_1,
  input  in_2,
  input  in_3,
  input  in_4
);

  Hex_Digit_Display hex_digit_display_1 ();  // open: value, dp

  // Other names for the same wires on the sheet: A = in_1; B = in_2; C = in_3; D = in_4
endmodule

module ha (
  input  x,
  input  y,
  output C_out,
  output O
);

  and and_1 (C_out, x, y);
  xor xor_1 (O, x, y);
endmodule
